// Logisim project mult4.circ as structural Verilog: 1 circuit, main circuit main
module main (
  input  A3,
  input  A2,
  input  A1,
  input  A0,
  input  B3,
  input  B2,
  input  B1,
  input  B0
);

  wire adder_1_cout, adder_1_out, adder_2_out, adder_3_out, and_1_out, and_2_out, and_3_out, and_4_out,
       and_5_out, and_6_out;

  and and_1 (and_1_out, B0, A0);
  and and_2 (and_2_out, B0, A1);
  and and_3 (and_3_out, A0, B1);
  and and_4 (and_4_out, A2, B0);
  and and_5 (and_5_out, A1, B1);
  and and_6 (and_6_out, B2, A0);
  // AND_Gate and_7 has open pins: in0=A3, in1=B0, out=open
  // AND_Gate and_8 has open pins: in0=A2, in1=B1, out=open
  // AND_Gate and_9 has open pins: in0=A1, in1=B2, out=open
  // AND_Gate and_10 has open pins: in0=A0, in1=B3, out=open
  // AND_Gate and_11 has open pins: in0=A3, in1=B1, out=open
  // AND_Gate and_12 has open pins: in0=A2, in1=B2, out=open
  // AND_Gate and_13 has open pins: in0=A1, in1=B3, out=open
  // AND_Gate and_14 has open pins: in0=A3, in1=B2, out=open
  // AND_Gate and_15 has open pins: in0=A2, in1=B3, out=open
  // AND_Gate and_16 has open pins: in0=B3, in1=A3, out=open
  Adder #(.width(1)) adder_1 (.a(and_2_out), .b(and_3_out), .out(adder_1_out), .cin(1'b0), .cout(adder_1_cout));
  Adder #(.width(1)) adder_2 (.a(and_4_out), .b(and_5_out), .out(adder_2_out), .cin(1'b0));  // open: cout
  Adder #(.width(1)) adder_3 (.a(adder_2_out), .b(and_6_out), .out(adder_3_out), .cin(adder_1_cout));  // open: cout
endmodule
